# Fritzing sketch ritournelle_sur_breadboard (saved by Fritzing 0.9.3b)
breadboards: 2

parts:
  Composant1 = Arduino Nano (Rev3.0)
  IC1 = IC, DIP package, 14 pins [chip_label=4066]
  IC2 = IC, DIP package, 14 pins [chip_label=4066]
  IC3 = IC, DIP package, 14 pins [chip_label=4066]
  IC4 = IC, DIP package, 14 pins [chip_label=4066]
  IC5 = IC, DIP package, 8 pins [chip_label=6N138]
  LED1 = LED - 3mm [color="Red (660nm)" package="3 mm [THT]"]
  R1 = Resistor [tolerance=±5% resistance=220 package=THT]
  R2 = Resistor [tolerance=±5% resistance=220 package=THT]
  D1 = Rectifier Diode [part_number=1N4148 package="300 mil [THT]"]
  R3 = Resistor [tolerance=±5% resistance=270 package=THT]
  J1 = male pin header, 8 pins [form="♂ (male)"]
  J2 = male pin header, 8 pins [form="♂ (male)"]
  J3 = male pin header, 8 pins [form="♂ (male)"]
  J4 = male pin header, 8 pins [form="♂ (male)"]

nets:
  N1: Composant1.GND, IC1.pin7, IC2.pin7, IC3.pin7, IC4.pin7, IC5.pin5, LED1.cathode
  N2: Composant1.D2, IC5.pin6, R3.Pin_1
  N3: Composant1.D3, R2.Pin_0
  N4: Composant1.D4, IC1.pin13
  N5: Composant1.D5, IC1.pin12
  N6: Composant1.D6, IC1.pin6
  N7: Composant1.D7, IC1.pin5
  N8: Composant1.D8, IC2.pin13
  N9: Composant1.D9, IC2.pin12
  N10: Composant1.D10, IC2.pin6
  N11: Composant1.D11/MOSI, IC2.pin5
  N12: Composant1.D12/MISO, IC3.pin13
  N13: Composant1.5V, IC1.pin14, IC2.pin14, IC3.pin14, IC4.pin14, IC5.pin8, R3.Pin_0
  N14: Composant1.A5, IC4.pin5
  N15: Composant1.A4, IC4.pin6
  N16: Composant1.A3, IC4.pin12
  N17: Composant1.A2, IC4.pin13
  N18: Composant1.A1, IC3.pin5
  N19: Composant1.A0, IC3.pin6
  N20: Composant1.D13/SCK, IC3.pin12
  N21: IC1.pin1, J1.pin1
  N22: IC1.pin2, J1.pin2
  N23: IC1.pin3, J1.pin7
  N24: IC1.pin4, J1.pin8
  N25: IC1.pin8, J1.pin6
  N26: IC1.pin9, J1.pin5
  N27: IC1.pin10, J1.pin4
  N28: IC1.pin11, J1.pin3
  N29: IC2.pin1, J2.pin1
  N30: IC2.pin2, J2.pin2
  N31: IC2.pin3, J2.pin7
  N32: IC2.pin4, J2.pin8
  N33: IC2.pin8, J2.pin6
  N34: IC2.pin9, J2.pin5
  N35: IC2.pin10, J2.pin4
  N36: IC2.pin11, J2.pin3
  N37: IC3.pin1, J3.pin1
  N38: IC3.pin2, J3.pin2
  N39: IC3.pin3, J3.pin7
  N40: IC3.pin4, J3.pin8
  N41: IC3.pin8, J3.pin6
  N42: IC3.pin9, J3.pin5
  N43: IC3.pin10, J3.pin4
  N44: IC3.pin11, J3.pin3
  N45: IC4.pin1, J4.pin1
  N46: IC4.pin2, J4.pin2
  N47: IC4.pin3, J4.pin7
  N48: IC4.pin4, J4.pin8
  N49: IC4.pin8, J4.pin6
  N50: IC4.pin9, J4.pin5
  N51: IC4.pin10, J4.pin4
  N52: IC4.pin11, J4.pin3
  N53: IC5.pin2, R1.Pin_0, D1.cathode
  N54: IC5.pin3, D1.anode
  N55: LED1.anode, R2.Pin_1

notes:
  broche MIDI 4
  broche MIDI 5
  270 Ω
  220 Ω
  1N4148
  connecteur de masse
  16 paires de fils à connecter
  aux boutons à remplacer
