# Fritzing sketch testeur_midi_sur_breadboard (saved by Fritzing 0.9.3b)
breadboards: 1

parts:
  Composant1 = Arduino Nano (Rev3.0)
  LED1 = LED - 5mm [color="Red (660nm)" package="5 mm [THT]"]
  R1 = Resistor [tolerance=±5% resistance=220 package=THT]
  R2 = Resistor [tolerance=±5% resistance=220 package=THT]

nets:
  N1: Composant1.GND, LED1.cathode
  N2: Composant1.D7, R1.Pin_0
  N3: Composant1.5V, R2.Pin_0
  N4: LED1.anode, R1.Pin_1

notes:
  vers connection MIDI 5
  vers connection MIDI 4
  vers connection MIDI 2
  R220
